// Logisim project branch-comp.circ as structural Verilog: 1 circuit, main circuit branch_comp
module branch_comp (
  input  [31:0] BrData1,
  input  [31:0] BrData2,
  input  BrUn,
  output BrEq,
  output BrLt
);

  wire and_1_out, D1Eq_0, D2Eq_0, Less_or_Equal, multiplexer_3_out, not_5_out, not_8_out, or_1_out, or_2_out,
       or_3_out, or_5_out, Sign_Difference, Sign_Eq, Sign_result, Unsign_Eq, Unsign_left_result,
       Unsign_result;
  wire [31:0] bit_extender_3_out, bit_extender_4_out, subtractor_2_out, xor_1_out, xor_2_out, xor_3_out;
  wire [32:0] bit_extender_1_out, bit_extender_2_out, subtractor_1_out;

  and and_1 (and_1_out, D1Eq_0, D2Eq_0);
  assign xor_1_out = BrData1 ^ BrData2;  // XOR_Gate xor_1, 32 bits wide
  assign xor_2_out = BrData1 ^ {32{1'b0}};  // XOR_Gate xor_2, 32 bits wide
  assign xor_3_out = BrData2 ^ {32{1'b0}};  // XOR_Gate xor_3, 32 bits wide
  or or_1 (or_1_out, xor_1_out[0], xor_1_out[1], xor_1_out[2], xor_1_out[3], xor_1_out[4], xor_1_out[5], xor_1_out[6], xor_1_out[7], xor_1_out[8], xor_1_out[9], xor_1_out[10], xor_1_out[11], xor_1_out[12], xor_1_out[13], xor_1_out[14], xor_1_out[15], xor_1_out[17], xor_1_out[18], xor_1_out[19], xor_1_out[20], xor_1_out[21], xor_1_out[22], xor_1_out[23], xor_1_out[24], xor_1_out[25], xor_1_out[26], xor_1_out[27], xor_1_out[28], xor_1_out[29], xor_1_out[30], xor_1_out[31], xor_1_out[16]);
  or or_2 (or_2_out, xor_2_out[0], xor_2_out[1], xor_2_out[2], xor_2_out[3], xor_2_out[4], xor_2_out[5], xor_2_out[6], xor_2_out[7], xor_2_out[8], xor_2_out[9], xor_2_out[10], xor_2_out[11], xor_2_out[12], xor_2_out[13], xor_2_out[14], xor_2_out[15], xor_2_out[17], xor_2_out[18], xor_2_out[19], xor_2_out[20], xor_2_out[21], xor_2_out[22], xor_2_out[23], xor_2_out[24], xor_2_out[25], xor_2_out[26], xor_2_out[27], xor_2_out[28], xor_2_out[29], xor_2_out[30], xor_2_out[16]);
  or or_3 (or_3_out, xor_3_out[0], xor_3_out[1], xor_3_out[2], xor_3_out[3], xor_3_out[4], xor_3_out[5], xor_3_out[6], xor_3_out[7], xor_3_out[8], xor_3_out[9], xor_3_out[10], xor_3_out[11], xor_3_out[12], xor_3_out[13], xor_3_out[14], xor_3_out[15], xor_3_out[17], xor_3_out[18], xor_3_out[19], xor_3_out[20], xor_3_out[21], xor_3_out[22], xor_3_out[23], xor_3_out[24], xor_3_out[25], xor_3_out[26], xor_3_out[27], xor_3_out[28], xor_3_out[29], xor_3_out[30], xor_3_out[16]);
  or or_4 (Sign_Eq, and_1_out, Unsign_Eq);
  not not_1 (Unsign_Eq, or_1_out);
  not not_2 (D1Eq_0, or_2_out);
  not not_3 (D2Eq_0, or_3_out);
  assign bit_extender_1_out = {{1{1'b1}}, BrData1};  // Bit_Extender bit_extender_1
  assign bit_extender_2_out = {{1{1'b0}}, BrData2};  // Bit_Extender bit_extender_2
  Subtractor #(.width(33)) subtractor_1 (
    .a(bit_extender_1_out), .b(bit_extender_2_out), .out(subtractor_1_out));  // open: bin, bout
  not not_4 (Unsign_result, subtractor_1_out[32]);
  assign bit_extender_3_out = {{1{1'b1}}, BrData1[30:0]};  // Bit_Extender bit_extender_3
  assign bit_extender_4_out = {{1{1'b0}}, BrData2[30:0]};  // Bit_Extender bit_extender_4
  xor xor_4 (Sign_Difference, BrData1[31], BrData2[31]);
  not not_5 (not_5_out, Less_or_Equal);
  Multiplexer multiplexer_1 (.in0(Unsign_Eq), .in1(Sign_Eq), .out(BrEq), .sel(BrUn));
  Subtractor #(.width(32)) subtractor_2 (
    .a(bit_extender_3_out), .b(bit_extender_4_out), .out(subtractor_2_out));  // open: bin, bout
  or or_5 (or_5_out, not_5_out, Sign_Eq);
  not not_6 (Sign_result, or_5_out);
  not not_7 (Unsign_left_result, subtractor_2_out[31]);
  Multiplexer multiplexer_2 (.in0(Unsign_result), .in1(Sign_result), .out(BrLt), .sel(BrUn));
  Multiplexer multiplexer_3 (.in0(Unsign_left_result), .in1(not_8_out), .out(multiplexer_3_out), .sel(BrData1[31]));
  not not_8 (not_8_out, Unsign_left_result);
  Multiplexer multiplexer_4 (.in0(multiplexer_3_out), .in1(BrData1[31]), .out(Less_or_Equal), .sel(Sign_Difference));

  // Other names for the same wires on the sheet: Sign_1 = BrData1[31]; Sign_2 = BrData2[31]

  // Notes on the sheet:
  //   INPUTS to your circuit
  //   DON'T CHANGE THE LOCATIONS OF THE INPUTS AND OUTPUTS!
  //   1 for negative 0 for possitive
  //   1 for different sign
  //   1 for negative 0 for possitive
  //   OUTPUT from your circuit
  //   1 for negative 0 for possitive
endmodule
