// Logisim project control-logic.circ as structural Verilog: 1 circuit, main circuit control_logic
module control_logic (
  input  [31:0] Instruction,
  input  BrEq,
  input  BrLt,
  output PCSel,
  output RegWEn,
  output [2:0] ImmSel,
  output BrUn,
  output ASel,
  output BSel,
  output [3:0] ALUSel,
  output MemWEn,
  output [1:0] WBSel
);

  wire and_9_out, and_10_out, and_11_out, and_12_out, and_13_out, and_14_out, is_add, is_addi, is_and,
       is_andi, is_auipc, is_beq, is_bge, is_bgeu, is_blt, is_bltu, is_bne, is_jal, is_jalr, is_lb, is_lh,
       is_lui, is_lw, is_mul, is_mulh, is_mulhu, is_none1, is_none2, is_none3, is_none4, is_or, is_ori,
       is_sb, is_sh, is_sll, is_slli, is_slt, is_slti, is_sra, is_srai, is_srl, is_srli, is_sub, is_sw,
       is_xor, is_xori, not_1_out, not_2_out, not_3_out, not_4_out, not_5_out, not_6_out, not_7_out,
       not_8_out, not_9_out, not_10_out, not_11_out, not_12_out, not_13_out, not_14_out, not_15_out,
       not_16_out, not_17_out, not_18_out, not_19_out, not_20_out, not_21_out, not_22_out, not_23_out,
       not_24_out, not_25_out, not_26_out, not_27_out, not_28_out, not_29_out, not_30_out, not_31_out,
       not_32_out, not_33_out, not_34_out, not_35_out, not_37_out, not_38_out, not_41_out, not_42_out,
       not_43_out, not_44_out, not_45_out, not_46_out, not_47_out, not_48_out, not_50_out, not_51_out,
       not_53_out, not_54_out, not_55_out, not_56_out, not_57_out, not_59_out, not_60_out, not_61_out,
       not_62_out, not_63_out, not_65_out, not_66_out, not_68_out, not_69_out, not_70_out, not_71_out,
       not_72_out, not_74_out, not_75_out, not_77_out, not_78_out, not_80_out, not_81_out, not_83_out,
       not_84_out, not_86_out, not_87_out, not_89_out, not_90_out, not_92_out, not_93_out, not_95_out,
       not_96_out, not_98_out, not_99_out, not_100_out, not_101_out, not_104_out, not_107_out, not_108_out,
       not_109_out, not_110_out, not_111_out, not_112_out, not_113_out, not_116_out, not_117_out,
       not_119_out, not_120_out, not_121_out, not_122_out, not_123_out, not_124_out, or_1_out, or_2_out,
       or_3_out, or_4_out, or_5_out, or_6_out, or_7_out, or_8_out, or_9_out, or_10_out, or_11_out, or_12_out,
       or_13_out, or_14_out, or_15_out, or_16_out, or_17_out, or_18_out, or_19_out, or_20_out, or_21_out,
       or_22_out, or_23_out, or_24_out, or_25_out, or_26_out, or_27_out, or_28_out, or_29_out, or_30_out,
       or_31_out, or_32_out, or_33_out, or_34_out, or_35_out, or_36_out, or_37_out, or_38_out, or_39_out,
       or_40_out, or_41_out, or_42_out, or_43_out, or_44_out, or_45_out, or_46_out, or_47_out, or_48_out,
       or_49_out, or_50_out, or_51_out, or_52_out, or_53_out, or_54_out, or_55_out, or_56_out, or_57_out,
       or_58_out, or_59_out, or_60_out, or_61_out, or_62_out, or_63_out, or_64_out, or_65_out, or_66_out,
       or_67_out, or_68_out, or_69_out, or_70_out, or_71_out, or_72_out, or_73_out, or_74_out, or_75_out,
       or_76_out, or_77_out, or_78_out, or_79_out, or_80_out, or_81_out, or_82_out, or_83_out, or_84_out,
       or_85_out, or_86_out, or_87_out, or_88_out, or_89_out, or_90_out, or_91_out, or_92_out, or_93_out,
       or_94_out, or_95_out, or_96_out, or_97_out, or_98_out, or_99_out, or_100_out, or_101_out, or_102_out,
       or_103_out, or_104_out, or_105_out, or_106_out, or_107_out, or_108_out, or_109_out, or_110_out,
       or_111_out, or_112_out, or_113_out, or_114_out, or_115_out, or_116_out, or_117_out, or_118_out,
       or_119_out, or_120_out, or_121_out, or_122_out, or_123_out;
  wire [2:0] xor_2_out, xor_5_out, xor_8_out, xor_11_out, xor_14_out, xor_17_out, xor_20_out, xor_23_out,
       xor_26_out, xor_29_out, xor_32_out, xor_35_out, xor_38_out, xor_41_out, xor_44_out, xor_47_out,
       xor_50_out, xor_53_out, xor_56_out, xor_59_out, xor_62_out, xor_65_out, xor_68_out, xor_71_out,
       xor_74_out, xor_77_out, xor_80_out, xor_83_out, xor_86_out, xor_89_out, xor_92_out, xor_95_out,
       xor_98_out, xor_101_out, xor_104_out, xor_107_out, xor_110_out, xor_113_out, xor_116_out, xor_119_out;
  wire [5:0] Rom_Input;
  wire [6:0] xor_1_out, xor_3_out, xor_4_out, xor_6_out, xor_7_out, xor_9_out, xor_10_out, xor_12_out,
       xor_13_out, xor_15_out, xor_16_out, xor_18_out, xor_19_out, xor_21_out, xor_22_out, xor_24_out,
       xor_25_out, xor_27_out, xor_28_out, xor_30_out, xor_31_out, xor_33_out, xor_34_out, xor_36_out,
       xor_37_out, xor_39_out, xor_40_out, xor_42_out, xor_43_out, xor_45_out, xor_46_out, xor_48_out,
       xor_49_out, xor_51_out, xor_52_out, xor_54_out, xor_55_out, xor_57_out, xor_58_out, xor_60_out,
       xor_61_out, xor_63_out, xor_64_out, xor_66_out, xor_67_out, xor_69_out, xor_70_out, xor_72_out,
       xor_73_out, xor_75_out, xor_76_out, xor_78_out, xor_79_out, xor_81_out, xor_82_out, xor_84_out,
       xor_85_out, xor_87_out, xor_88_out, xor_90_out, xor_91_out, xor_93_out, xor_94_out, xor_96_out,
       xor_97_out, xor_99_out, xor_100_out, xor_102_out, xor_103_out, xor_105_out, xor_106_out, xor_108_out,
       xor_109_out, xor_111_out, xor_112_out, xor_114_out, xor_115_out, xor_117_out, xor_118_out, xor_120_out;
  wire [15:14] rom_1_data;

  assign xor_1_out = Instruction[6:0] ^ 7'b0110011;  // XOR_Gate xor_1, 7 bits wide
  assign xor_2_out = Instruction[14:12] ^ 3'b000;  // XOR_Gate xor_2, 3 bits wide
  assign xor_3_out = Instruction[31:25] ^ {7{1'b0}};  // XOR_Gate xor_3, 7 bits wide
  assign xor_4_out = Instruction[6:0] ^ 7'b0110011;  // XOR_Gate xor_4, 7 bits wide
  assign xor_5_out = Instruction[14:12] ^ 3'b000;  // XOR_Gate xor_5, 3 bits wide
  assign xor_6_out = Instruction[31:25] ^ 7'b0100000;  // XOR_Gate xor_6, 7 bits wide
  assign xor_7_out = Instruction[6:0] ^ 7'b0110011;  // XOR_Gate xor_7, 7 bits wide
  assign xor_8_out = Instruction[14:12] ^ 3'b001;  // XOR_Gate xor_8, 3 bits wide
  assign xor_9_out = Instruction[31:25] ^ 7'b0000001;  // XOR_Gate xor_9, 7 bits wide
  assign xor_10_out = Instruction[6:0] ^ 7'b0110011;  // XOR_Gate xor_10, 7 bits wide
  assign xor_11_out = Instruction[14:12] ^ 3'b010;  // XOR_Gate xor_11, 3 bits wide
  assign xor_12_out = Instruction[31:25] ^ {7{1'b0}};  // XOR_Gate xor_12, 7 bits wide
  or or_1 (or_1_out, xor_1_out[0], xor_1_out[1], xor_1_out[2], xor_1_out[3], xor_1_out[4], xor_1_out[5], xor_1_out[6]);
  not not_1 (not_1_out, or_1_out);
  or or_2 (or_2_out, xor_2_out[0], xor_2_out[1], xor_2_out[2]);
  not not_2 (not_2_out, or_2_out);
  or or_3 (or_3_out, xor_3_out[0], xor_3_out[1], xor_3_out[2], xor_3_out[3], xor_3_out[4], xor_3_out[5], xor_3_out[6]);
  not not_3 (not_3_out, or_3_out);
  or or_4 (or_4_out, xor_4_out[0], xor_4_out[1], xor_4_out[2], xor_4_out[3], xor_4_out[4], xor_4_out[5], xor_4_out[6]);
  not not_4 (not_4_out, or_4_out);
  or or_5 (or_5_out, xor_5_out[0], xor_5_out[1], xor_5_out[2]);
  not not_5 (not_5_out, or_5_out);
  or or_6 (or_6_out, xor_6_out[0], xor_6_out[1], xor_6_out[2], xor_6_out[3], xor_6_out[4], xor_6_out[5], xor_6_out[6]);
  not not_6 (not_6_out, or_6_out);
  or or_7 (or_7_out, xor_7_out[0], xor_7_out[1], xor_7_out[2], xor_7_out[3], xor_7_out[4], xor_7_out[5], xor_7_out[6]);
  not not_7 (not_7_out, or_7_out);
  or or_8 (or_8_out, xor_8_out[0], xor_8_out[1], xor_8_out[2]);
  not not_8 (not_8_out, or_8_out);
  or or_9 (or_9_out, xor_9_out[0], xor_9_out[1], xor_9_out[2], xor_9_out[3], xor_9_out[4], xor_9_out[5], xor_9_out[6]);
  not not_9 (not_9_out, or_9_out);
  or or_10 (or_10_out, xor_10_out[0], xor_10_out[1], xor_10_out[2], xor_10_out[3], xor_10_out[4], xor_10_out[5], xor_10_out[6]);
  not not_10 (not_10_out, or_10_out);
  or or_11 (or_11_out, xor_11_out[0], xor_11_out[1], xor_11_out[2]);
  not not_11 (not_11_out, or_11_out);
  or or_12 (or_12_out, xor_12_out[0], xor_12_out[1], xor_12_out[2], xor_12_out[3], xor_12_out[4], xor_12_out[5], xor_12_out[6]);
  not not_12 (not_12_out, or_12_out);
  ROM #(.addrWidth(6), .dataWidth(16)) rom_1 (
    .addr(Rom_Input), .data({rom_1_data, WBSel, MemWEn, ALUSel, BSel, ASel, BrUn, ImmSel, RegWEn}));
  and and_1 (is_add, not_1_out, not_2_out, not_3_out);
  and and_2 (is_sub, not_4_out, not_5_out, not_6_out);
  and and_3 (is_mulh, not_7_out, not_8_out, not_9_out);
  and and_4 (is_slt, not_10_out, not_11_out, not_12_out);
  assign xor_13_out = Instruction[6:0] ^ 7'b0110011;  // XOR_Gate xor_13, 7 bits wide
  assign xor_14_out = Instruction[14:12] ^ 3'b000;  // XOR_Gate xor_14, 3 bits wide
  assign xor_15_out = Instruction[31:25] ^ 7'b0000001;  // XOR_Gate xor_15, 7 bits wide
  assign xor_16_out = Instruction[6:0] ^ 7'b0110011;  // XOR_Gate xor_16, 7 bits wide
  assign xor_17_out = Instruction[14:12] ^ 3'b001;  // XOR_Gate xor_17, 3 bits wide
  assign xor_18_out = Instruction[31:25] ^ {7{1'b0}};  // XOR_Gate xor_18, 7 bits wide
  assign xor_19_out = Instruction[6:0] ^ 7'b0110011;  // XOR_Gate xor_19, 7 bits wide
  assign xor_20_out = Instruction[14:12] ^ 3'b011;  // XOR_Gate xor_20, 3 bits wide
  assign xor_21_out = Instruction[31:25] ^ 7'b0000001;  // XOR_Gate xor_21, 7 bits wide
  assign xor_22_out = Instruction[6:0] ^ 7'b0110011;  // XOR_Gate xor_22, 7 bits wide
  assign xor_23_out = Instruction[14:12] ^ 3'b100;  // XOR_Gate xor_23, 3 bits wide
  assign xor_24_out = Instruction[31:25] ^ {7{1'b0}};  // XOR_Gate xor_24, 7 bits wide
  Priority_Encoder #(.select_enc(6)) priority_encoder_1 (
    .in0(is_add), .in1(is_mul), .in2(is_sub), .in3(is_sll), .in4(is_mulh), .in5(is_mulhu), .in6(is_slt),
    .in7(is_xor), .in8(is_srl), .in9(is_sra), .in10(is_or), .in11(is_and), .in12(is_lb), .in13(is_lh),
    .in14(is_lw), .in15(is_addi), .in16(is_slli), .in17(is_slti), .in18(is_xori), .in19(is_srli),
    .in20(is_srai), .in21(is_ori), .in22(is_andi), .in23(is_sb), .in24(is_sh), .in25(is_sw), .in26(is_beq),
    .in27(is_bne), .in28(is_blt), .in29(is_bge), .in30(is_bltu), .in31(is_bgeu), .in32(is_auipc),
    .in33(is_lui), .in34(is_jal), .in35(is_jalr), .out(Rom_Input));  // open: in36, in37, in38, in39, in40, in41, in42, in43, in44, in45, in46, in47, in48, in49, in50, in51, in52, in53, in54, in55, in56, in57, in58, in59, in60, in61, in62, in63, gs, en_out, en_in
  or or_13 (or_13_out, xor_13_out[0], xor_13_out[1], xor_13_out[2], xor_13_out[3], xor_13_out[4], xor_13_out[5], xor_13_out[6]);
  or or_14 (or_14_out, xor_14_out[0], xor_14_out[1], xor_14_out[2]);
  or or_15 (or_15_out, xor_15_out[0], xor_15_out[1], xor_15_out[2], xor_15_out[3], xor_15_out[4], xor_15_out[5], xor_15_out[6]);
  or or_16 (or_16_out, xor_16_out[0], xor_16_out[1], xor_16_out[2], xor_16_out[3], xor_16_out[4], xor_16_out[5], xor_16_out[6]);
  or or_17 (or_17_out, xor_17_out[0], xor_17_out[1], xor_17_out[2]);
  or or_18 (or_18_out, xor_18_out[0], xor_18_out[1], xor_18_out[2], xor_18_out[3], xor_18_out[4], xor_18_out[5], xor_18_out[6]);
  or or_19 (or_19_out, xor_19_out[0], xor_19_out[1], xor_19_out[2], xor_19_out[3], xor_19_out[4], xor_19_out[5], xor_19_out[6]);
  or or_20 (or_20_out, xor_20_out[0], xor_20_out[1], xor_20_out[2]);
  or or_21 (or_21_out, xor_21_out[0], xor_21_out[1], xor_21_out[2], xor_21_out[3], xor_21_out[4], xor_21_out[5], xor_21_out[6]);
  or or_22 (or_22_out, xor_22_out[0], xor_22_out[1], xor_22_out[2], xor_22_out[3], xor_22_out[4], xor_22_out[5], xor_22_out[6]);
  or or_23 (or_23_out, xor_23_out[0], xor_23_out[1], xor_23_out[2]);
  or or_24 (or_24_out, xor_24_out[0], xor_24_out[1], xor_24_out[2], xor_24_out[3], xor_24_out[4], xor_24_out[5], xor_24_out[6]);
  not not_13 (not_13_out, or_13_out);
  not not_14 (not_14_out, or_14_out);
  not not_15 (not_15_out, or_15_out);
  not not_16 (not_16_out, or_16_out);
  not not_17 (not_17_out, or_17_out);
  not not_18 (not_18_out, or_18_out);
  not not_19 (not_19_out, or_19_out);
  not not_20 (not_20_out, or_20_out);
  not not_21 (not_21_out, or_21_out);
  not not_22 (not_22_out, or_22_out);
  not not_23 (not_23_out, or_23_out);
  not not_24 (not_24_out, or_24_out);
  and and_5 (is_mul, not_13_out, not_14_out, not_15_out);
  and and_6 (is_sll, not_16_out, not_17_out, not_18_out);
  and and_7 (is_mulhu, not_19_out, not_20_out, not_21_out);
  and and_8 (is_xor, not_22_out, not_23_out, not_24_out);
  not not_25 (not_25_out, BrEq);
  not not_26 (not_26_out, BrLt);
  not not_27 (not_27_out, BrLt);
  and and_9 (and_9_out, BrEq, is_beq);
  and and_10 (and_10_out, not_25_out, is_bne);
  and and_11 (and_11_out, BrLt, is_blt);
  or or_25 (or_25_out, not_26_out, BrEq);
  and and_12 (and_12_out, BrLt, is_bltu);
  or or_26 (or_26_out, not_27_out, BrEq);
  assign xor_25_out = Instruction[6:0] ^ 7'b0110011;  // XOR_Gate xor_25, 7 bits wide
  assign xor_26_out = Instruction[14:12] ^ 3'b101;  // XOR_Gate xor_26, 3 bits wide
  assign xor_27_out = Instruction[31:25] ^ {7{1'b0}};  // XOR_Gate xor_27, 7 bits wide
  assign xor_28_out = Instruction[6:0] ^ 7'b0110011;  // XOR_Gate xor_28, 7 bits wide
  assign xor_29_out = Instruction[14:12] ^ 3'b110;  // XOR_Gate xor_29, 3 bits wide
  assign xor_30_out = Instruction[31:25] ^ {7{1'b0}};  // XOR_Gate xor_30, 7 bits wide
  assign xor_31_out = Instruction[6:0] ^ 7'b0000011;  // XOR_Gate xor_31, 7 bits wide
  assign xor_32_out = Instruction[14:12] ^ 3'b000;  // XOR_Gate xor_32, 3 bits wide
  assign xor_33_out = Instruction[31:25] ^ {7{1'b0}};  // XOR_Gate xor_33, 7 bits wide
  assign xor_34_out = Instruction[6:0] ^ 7'b0000011;  // XOR_Gate xor_34, 7 bits wide
  assign xor_35_out = Instruction[14:12] ^ 3'b010;  // XOR_Gate xor_35, 3 bits wide
  assign xor_36_out = Instruction[31:25] ^ {7{1'b0}};  // XOR_Gate xor_36, 7 bits wide
  and and_13 (and_13_out, or_25_out, is_bge);
  and and_14 (and_14_out, or_26_out, is_bgeu);
  or or_27 (or_27_out, xor_25_out[0], xor_25_out[1], xor_25_out[2], xor_25_out[3], xor_25_out[4], xor_25_out[5], xor_25_out[6]);
  not not_28 (not_28_out, or_27_out);
  or or_28 (or_28_out, xor_26_out[0], xor_26_out[1], xor_26_out[2]);
  not not_29 (not_29_out, or_28_out);
  or or_29 (or_29_out, xor_27_out[0], xor_27_out[1], xor_27_out[2], xor_27_out[3], xor_27_out[4], xor_27_out[5], xor_27_out[6]);
  not not_30 (not_30_out, or_29_out);
  or or_30 (or_30_out, xor_28_out[0], xor_28_out[1], xor_28_out[2], xor_28_out[3], xor_28_out[4], xor_28_out[5], xor_28_out[6]);
  not not_31 (not_31_out, or_30_out);
  or or_31 (or_31_out, xor_29_out[0], xor_29_out[1], xor_29_out[2]);
  not not_32 (not_32_out, or_31_out);
  or or_32 (or_32_out, xor_30_out[0], xor_30_out[1], xor_30_out[2], xor_30_out[3], xor_30_out[4], xor_30_out[5], xor_30_out[6]);
  not not_33 (not_33_out, or_32_out);
  or or_33 (or_33_out, xor_31_out[0], xor_31_out[1], xor_31_out[2], xor_31_out[3], xor_31_out[4], xor_31_out[5], xor_31_out[6]);
  not not_34 (not_34_out, or_33_out);
  or or_34 (or_34_out, xor_32_out[0], xor_32_out[1], xor_32_out[2]);
  not not_35 (not_35_out, or_34_out);
  or or_35 (or_35_out, xor_33_out[0], xor_33_out[1], xor_33_out[2], xor_33_out[3], xor_33_out[4], xor_33_out[5], xor_33_out[6]);
  // NOT_Gate not_36 has open pins: in=or_35_out, out=open
  or or_36 (or_36_out, xor_34_out[0], xor_34_out[1], xor_34_out[2], xor_34_out[3], xor_34_out[4], xor_34_out[5], xor_34_out[6]);
  not not_37 (not_37_out, or_36_out);
  or or_37 (or_37_out, xor_35_out[0], xor_35_out[1], xor_35_out[2]);
  not not_38 (not_38_out, or_37_out);
  or or_38 (or_38_out, xor_36_out[0], xor_36_out[1], xor_36_out[2], xor_36_out[3], xor_36_out[4], xor_36_out[5], xor_36_out[6]);
  // NOT_Gate not_39 has open pins: in=or_38_out, out=open
  and and_15 (is_srl, not_28_out, not_29_out, not_30_out);
  and and_16 (is_or, not_31_out, not_32_out, not_33_out);
  and and_17 (is_lb, not_34_out, not_35_out);
  and and_18 (is_lw, not_37_out, not_38_out);
  or or_39 (or_39_out, and_9_out, and_10_out, and_11_out, and_13_out, and_12_out, and_14_out, is_jal, is_jalr);
  not not_40 (PCSel, or_39_out);
  assign xor_37_out = Instruction[6:0] ^ 7'b0110011;  // XOR_Gate xor_37, 7 bits wide
  assign xor_38_out = Instruction[14:12] ^ 3'b101;  // XOR_Gate xor_38, 3 bits wide
  assign xor_39_out = Instruction[31:25] ^ 7'b0100000;  // XOR_Gate xor_39, 7 bits wide
  assign xor_40_out = Instruction[6:0] ^ 7'b0110011;  // XOR_Gate xor_40, 7 bits wide
  assign xor_41_out = Instruction[14:12] ^ 3'b111;  // XOR_Gate xor_41, 3 bits wide
  assign xor_42_out = Instruction[31:25] ^ {7{1'b0}};  // XOR_Gate xor_42, 7 bits wide
  assign xor_43_out = Instruction[6:0] ^ 7'b0000011;  // XOR_Gate xor_43, 7 bits wide
  assign xor_44_out = Instruction[14:12] ^ 3'b001;  // XOR_Gate xor_44, 3 bits wide
  assign xor_45_out = Instruction[31:25] ^ {7{1'b0}};  // XOR_Gate xor_45, 7 bits wide
  assign xor_46_out = Instruction[6:0] ^ 7'b0010011;  // XOR_Gate xor_46, 7 bits wide
  assign xor_47_out = Instruction[14:12] ^ 3'b000;  // XOR_Gate xor_47, 3 bits wide
  assign xor_48_out = Instruction[31:25] ^ {7{1'b0}};  // XOR_Gate xor_48, 7 bits wide
  or or_40 (or_40_out, xor_37_out[0], xor_37_out[1], xor_37_out[2], xor_37_out[3], xor_37_out[4], xor_37_out[5], xor_37_out[6]);
  or or_41 (or_41_out, xor_38_out[0], xor_38_out[1], xor_38_out[2]);
  or or_42 (or_42_out, xor_39_out[0], xor_39_out[1], xor_39_out[2], xor_39_out[3], xor_39_out[4], xor_39_out[5], xor_39_out[6]);
  or or_43 (or_43_out, xor_40_out[0], xor_40_out[1], xor_40_out[2], xor_40_out[3], xor_40_out[4], xor_40_out[5], xor_40_out[6]);
  or or_44 (or_44_out, xor_41_out[0], xor_41_out[1], xor_41_out[2]);
  or or_45 (or_45_out, xor_42_out[0], xor_42_out[1], xor_42_out[2], xor_42_out[3], xor_42_out[4], xor_42_out[5], xor_42_out[6]);
  or or_46 (or_46_out, xor_43_out[0], xor_43_out[1], xor_43_out[2], xor_43_out[3], xor_43_out[4], xor_43_out[5], xor_43_out[6]);
  or or_47 (or_47_out, xor_44_out[0], xor_44_out[1], xor_44_out[2]);
  or or_48 (or_48_out, xor_45_out[0], xor_45_out[1], xor_45_out[2], xor_45_out[3], xor_45_out[4], xor_45_out[5], xor_45_out[6]);
  or or_49 (or_49_out, xor_46_out[0], xor_46_out[1], xor_46_out[2], xor_46_out[3], xor_46_out[4], xor_46_out[5], xor_46_out[6]);
  or or_50 (or_50_out, xor_47_out[0], xor_47_out[1], xor_47_out[2]);
  or or_51 (or_51_out, xor_48_out[0], xor_48_out[1], xor_48_out[2], xor_48_out[3], xor_48_out[4], xor_48_out[5], xor_48_out[6]);
  not not_41 (not_41_out, or_40_out);
  not not_42 (not_42_out, or_41_out);
  not not_43 (not_43_out, or_42_out);
  not not_44 (not_44_out, or_43_out);
  not not_45 (not_45_out, or_44_out);
  not not_46 (not_46_out, or_45_out);
  not not_47 (not_47_out, or_46_out);
  not not_48 (not_48_out, or_47_out);
  // NOT_Gate not_49 has open pins: in=or_48_out, out=open
  not not_50 (not_50_out, or_49_out);
  not not_51 (not_51_out, or_50_out);
  // NOT_Gate not_52 has open pins: in=or_51_out, out=open
  and and_19 (is_sra, not_41_out, not_42_out, not_43_out);
  and and_20 (is_and, not_44_out, not_45_out, not_46_out);
  and and_21 (is_lh, not_47_out, not_48_out);
  and and_22 (is_addi, not_50_out, not_51_out);
  assign xor_49_out = Instruction[6:0] ^ 7'b0010011;  // XOR_Gate xor_49, 7 bits wide
  assign xor_50_out = Instruction[14:12] ^ 3'b001;  // XOR_Gate xor_50, 3 bits wide
  assign xor_51_out = Instruction[31:25] ^ {7{1'b0}};  // XOR_Gate xor_51, 7 bits wide
  assign xor_52_out = Instruction[6:0] ^ 7'b0010011;  // XOR_Gate xor_52, 7 bits wide
  assign xor_53_out = Instruction[14:12] ^ 3'b100;  // XOR_Gate xor_53, 3 bits wide
  assign xor_54_out = Instruction[31:25] ^ {7{1'b0}};  // XOR_Gate xor_54, 7 bits wide
  assign xor_55_out = Instruction[6:0] ^ 7'b0010011;  // XOR_Gate xor_55, 7 bits wide
  assign xor_56_out = Instruction[14:12] ^ 3'b101;  // XOR_Gate xor_56, 3 bits wide
  assign xor_57_out = Instruction[31:25] ^ 7'b0100000;  // XOR_Gate xor_57, 7 bits wide
  assign xor_58_out = Instruction[6:0] ^ 7'b0010011;  // XOR_Gate xor_58, 7 bits wide
  assign xor_59_out = Instruction[14:12] ^ 3'b111;  // XOR_Gate xor_59, 3 bits wide
  assign xor_60_out = Instruction[31:25] ^ {7{1'b0}};  // XOR_Gate xor_60, 7 bits wide
  or or_52 (or_52_out, xor_49_out[0], xor_49_out[1], xor_49_out[2], xor_49_out[3], xor_49_out[4], xor_49_out[5], xor_49_out[6]);
  not not_53 (not_53_out, or_52_out);
  or or_53 (or_53_out, xor_50_out[0], xor_50_out[1], xor_50_out[2]);
  not not_54 (not_54_out, or_53_out);
  or or_54 (or_54_out, xor_51_out[0], xor_51_out[1], xor_51_out[2], xor_51_out[3], xor_51_out[4], xor_51_out[5], xor_51_out[6]);
  not not_55 (not_55_out, or_54_out);
  or or_55 (or_55_out, xor_52_out[0], xor_52_out[1], xor_52_out[2], xor_52_out[3], xor_52_out[4], xor_52_out[5], xor_52_out[6]);
  not not_56 (not_56_out, or_55_out);
  or or_56 (or_56_out, xor_53_out[0], xor_53_out[1], xor_53_out[2]);
  not not_57 (not_57_out, or_56_out);
  or or_57 (or_57_out, xor_54_out[0], xor_54_out[1], xor_54_out[2], xor_54_out[3], xor_54_out[4], xor_54_out[5], xor_54_out[6]);
  // NOT_Gate not_58 has open pins: in=or_57_out, out=open
  or or_58 (or_58_out, xor_55_out[0], xor_55_out[1], xor_55_out[2], xor_55_out[3], xor_55_out[4], xor_55_out[5], xor_55_out[6]);
  not not_59 (not_59_out, or_58_out);
  or or_59 (or_59_out, xor_56_out[0], xor_56_out[1], xor_56_out[2]);
  not not_60 (not_60_out, or_59_out);
  or or_60 (or_60_out, xor_57_out[0], xor_57_out[1], xor_57_out[2], xor_57_out[3], xor_57_out[4], xor_57_out[5], xor_57_out[6]);
  not not_61 (not_61_out, or_60_out);
  or or_61 (or_61_out, xor_58_out[0], xor_58_out[1], xor_58_out[2], xor_58_out[3], xor_58_out[4], xor_58_out[5], xor_58_out[6]);
  not not_62 (not_62_out, or_61_out);
  or or_62 (or_62_out, xor_59_out[0], xor_59_out[1], xor_59_out[2]);
  not not_63 (not_63_out, or_62_out);
  or or_63 (or_63_out, xor_60_out[0], xor_60_out[1], xor_60_out[2], xor_60_out[3], xor_60_out[4], xor_60_out[5], xor_60_out[6]);
  // NOT_Gate not_64 has open pins: in=or_63_out, out=open
  and and_23 (is_slli, not_53_out, not_54_out, not_55_out);
  and and_24 (is_xori, not_56_out, not_57_out);
  and and_25 (is_srai, not_59_out, not_60_out, not_61_out);
  and and_26 (is_andi, not_62_out, not_63_out);
  assign xor_61_out = Instruction[6:0] ^ 7'b0010011;  // XOR_Gate xor_61, 7 bits wide
  assign xor_62_out = Instruction[14:12] ^ 3'b010;  // XOR_Gate xor_62, 3 bits wide
  assign xor_63_out = Instruction[31:25] ^ {7{1'b0}};  // XOR_Gate xor_63, 7 bits wide
  assign xor_64_out = Instruction[6:0] ^ 7'b0010011;  // XOR_Gate xor_64, 7 bits wide
  assign xor_65_out = Instruction[14:12] ^ 3'b101;  // XOR_Gate xor_65, 3 bits wide
  assign xor_66_out = Instruction[31:25] ^ {7{1'b0}};  // XOR_Gate xor_66, 7 bits wide
  assign xor_67_out = Instruction[6:0] ^ 7'b0010011;  // XOR_Gate xor_67, 7 bits wide
  assign xor_68_out = Instruction[14:12] ^ 3'b110;  // XOR_Gate xor_68, 3 bits wide
  assign xor_69_out = Instruction[31:25] ^ {7{1'b0}};  // XOR_Gate xor_69, 7 bits wide
  assign xor_70_out = Instruction[6:0] ^ 7'b0100011;  // XOR_Gate xor_70, 7 bits wide
  assign xor_71_out = Instruction[14:12] ^ 3'b000;  // XOR_Gate xor_71, 3 bits wide
  assign xor_72_out = Instruction[31:25] ^ {7{1'b0}};  // XOR_Gate xor_72, 7 bits wide
  or or_64 (or_64_out, xor_61_out[0], xor_61_out[1], xor_61_out[2], xor_61_out[3], xor_61_out[4], xor_61_out[5], xor_61_out[6]);
  not not_65 (not_65_out, or_64_out);
  or or_65 (or_65_out, xor_62_out[0], xor_62_out[1], xor_62_out[2]);
  not not_66 (not_66_out, or_65_out);
  or or_66 (or_66_out, xor_63_out[0], xor_63_out[1], xor_63_out[2], xor_63_out[3], xor_63_out[4], xor_63_out[5], xor_63_out[6]);
  // NOT_Gate not_67 has open pins: in=or_66_out, out=open
  or or_67 (or_67_out, xor_64_out[0], xor_64_out[1], xor_64_out[2], xor_64_out[3], xor_64_out[4], xor_64_out[5], xor_64_out[6]);
  not not_68 (not_68_out, or_67_out);
  or or_68 (or_68_out, xor_65_out[0], xor_65_out[1], xor_65_out[2]);
  not not_69 (not_69_out, or_68_out);
  or or_69 (or_69_out, xor_66_out[0], xor_66_out[1], xor_66_out[2], xor_66_out[3], xor_66_out[4], xor_66_out[5], xor_66_out[6]);
  not not_70 (not_70_out, or_69_out);
  or or_70 (or_70_out, xor_67_out[0], xor_67_out[1], xor_67_out[2], xor_67_out[3], xor_67_out[4], xor_67_out[5], xor_67_out[6]);
  not not_71 (not_71_out, or_70_out);
  or or_71 (or_71_out, xor_68_out[0], xor_68_out[1], xor_68_out[2]);
  not not_72 (not_72_out, or_71_out);
  or or_72 (or_72_out, xor_69_out[0], xor_69_out[1], xor_69_out[2], xor_69_out[3], xor_69_out[4], xor_69_out[5], xor_69_out[6]);
  // NOT_Gate not_73 has open pins: in=or_72_out, out=open
  or or_73 (or_73_out, xor_70_out[0], xor_70_out[1], xor_70_out[2], xor_70_out[3], xor_70_out[4], xor_70_out[5], xor_70_out[6]);
  not not_74 (not_74_out, or_73_out);
  or or_74 (or_74_out, xor_71_out[0], xor_71_out[1], xor_71_out[2]);
  not not_75 (not_75_out, or_74_out);
  or or_75 (or_75_out, xor_72_out[0], xor_72_out[1], xor_72_out[2], xor_72_out[3], xor_72_out[4], xor_72_out[5], xor_72_out[6]);
  // NOT_Gate not_76 has open pins: in=or_75_out, out=open
  and and_27 (is_slti, not_65_out, not_66_out);
  and and_28 (is_srli, not_68_out, not_69_out, not_70_out);
  and and_29 (is_ori, not_71_out, not_72_out);
  and and_30 (is_sb, not_74_out, not_75_out);
  assign xor_73_out = Instruction[6:0] ^ 7'b0100011;  // XOR_Gate xor_73, 7 bits wide
  assign xor_74_out = Instruction[14:12] ^ 3'b001;  // XOR_Gate xor_74, 3 bits wide
  assign xor_75_out = Instruction[31:25] ^ {7{1'b0}};  // XOR_Gate xor_75, 7 bits wide
  assign xor_76_out = Instruction[6:0] ^ 7'b1100011;  // XOR_Gate xor_76, 7 bits wide
  assign xor_77_out = Instruction[14:12] ^ 3'b000;  // XOR_Gate xor_77, 3 bits wide
  assign xor_78_out = Instruction[31:25] ^ {7{1'b0}};  // XOR_Gate xor_78, 7 bits wide
  assign xor_79_out = Instruction[6:0] ^ 7'b1100011;  // XOR_Gate xor_79, 7 bits wide
  assign xor_80_out = Instruction[14:12] ^ 3'b100;  // XOR_Gate xor_80, 3 bits wide
  assign xor_81_out = Instruction[31:25] ^ {7{1'b0}};  // XOR_Gate xor_81, 7 bits wide
  assign xor_82_out = Instruction[6:0] ^ 7'b1100011;  // XOR_Gate xor_82, 7 bits wide
  assign xor_83_out = Instruction[14:12] ^ 3'b110;  // XOR_Gate xor_83, 3 bits wide
  assign xor_84_out = Instruction[31:25] ^ {7{1'b0}};  // XOR_Gate xor_84, 7 bits wide
  or or_76 (or_76_out, xor_73_out[0], xor_73_out[1], xor_73_out[2], xor_73_out[3], xor_73_out[4], xor_73_out[5], xor_73_out[6]);
  or or_77 (or_77_out, xor_74_out[0], xor_74_out[1], xor_74_out[2]);
  or or_78 (or_78_out, xor_75_out[0], xor_75_out[1], xor_75_out[2], xor_75_out[3], xor_75_out[4], xor_75_out[5], xor_75_out[6]);
  or or_79 (or_79_out, xor_76_out[0], xor_76_out[1], xor_76_out[2], xor_76_out[3], xor_76_out[4], xor_76_out[5], xor_76_out[6]);
  or or_80 (or_80_out, xor_77_out[0], xor_77_out[1], xor_77_out[2]);
  or or_81 (or_81_out, xor_78_out[0], xor_78_out[1], xor_78_out[2], xor_78_out[3], xor_78_out[4], xor_78_out[5], xor_78_out[6]);
  or or_82 (or_82_out, xor_79_out[0], xor_79_out[1], xor_79_out[2], xor_79_out[3], xor_79_out[4], xor_79_out[5], xor_79_out[6]);
  or or_83 (or_83_out, xor_80_out[0], xor_80_out[1], xor_80_out[2]);
  or or_84 (or_84_out, xor_81_out[0], xor_81_out[1], xor_81_out[2], xor_81_out[3], xor_81_out[4], xor_81_out[5], xor_81_out[6]);
  or or_85 (or_85_out, xor_82_out[0], xor_82_out[1], xor_82_out[2], xor_82_out[3], xor_82_out[4], xor_82_out[5], xor_82_out[6]);
  or or_86 (or_86_out, xor_83_out[0], xor_83_out[1], xor_83_out[2]);
  or or_87 (or_87_out, xor_84_out[0], xor_84_out[1], xor_84_out[2], xor_84_out[3], xor_84_out[4], xor_84_out[5], xor_84_out[6]);
  not not_77 (not_77_out, or_76_out);
  not not_78 (not_78_out, or_77_out);
  // NOT_Gate not_79 has open pins: in=or_78_out, out=open
  not not_80 (not_80_out, or_79_out);
  not not_81 (not_81_out, or_80_out);
  // NOT_Gate not_82 has open pins: in=or_81_out, out=open
  not not_83 (not_83_out, or_82_out);
  not not_84 (not_84_out, or_83_out);
  // NOT_Gate not_85 has open pins: in=or_84_out, out=open
  not not_86 (not_86_out, or_85_out);
  not not_87 (not_87_out, or_86_out);
  // NOT_Gate not_88 has open pins: in=or_87_out, out=open
  and and_31 (is_sh, not_77_out, not_78_out);
  and and_32 (is_beq, not_80_out, not_81_out);
  and and_33 (is_blt, not_83_out, not_84_out);
  and and_34 (is_bltu, not_86_out, not_87_out);
  assign xor_85_out = Instruction[6:0] ^ 7'b0100011;  // XOR_Gate xor_85, 7 bits wide
  assign xor_86_out = Instruction[14:12] ^ 3'b010;  // XOR_Gate xor_86, 3 bits wide
  assign xor_87_out = Instruction[31:25] ^ {7{1'b0}};  // XOR_Gate xor_87, 7 bits wide
  assign xor_88_out = Instruction[6:0] ^ 7'b1100011;  // XOR_Gate xor_88, 7 bits wide
  assign xor_89_out = Instruction[14:12] ^ 3'b001;  // XOR_Gate xor_89, 3 bits wide
  assign xor_90_out = Instruction[31:25] ^ {7{1'b0}};  // XOR_Gate xor_90, 7 bits wide
  assign xor_91_out = Instruction[6:0] ^ 7'b1100011;  // XOR_Gate xor_91, 7 bits wide
  assign xor_92_out = Instruction[14:12] ^ 3'b101;  // XOR_Gate xor_92, 3 bits wide
  assign xor_93_out = Instruction[31:25] ^ {7{1'b0}};  // XOR_Gate xor_93, 7 bits wide
  assign xor_94_out = Instruction[6:0] ^ 7'b1100011;  // XOR_Gate xor_94, 7 bits wide
  assign xor_95_out = Instruction[14:12] ^ 3'b111;  // XOR_Gate xor_95, 3 bits wide
  assign xor_96_out = Instruction[31:25] ^ {7{1'b0}};  // XOR_Gate xor_96, 7 bits wide
  or or_88 (or_88_out, xor_85_out[0], xor_85_out[1], xor_85_out[2], xor_85_out[3], xor_85_out[4], xor_85_out[5], xor_85_out[6]);
  not not_89 (not_89_out, or_88_out);
  or or_89 (or_89_out, xor_86_out[0], xor_86_out[1], xor_86_out[2]);
  not not_90 (not_90_out, or_89_out);
  or or_90 (or_90_out, xor_87_out[0], xor_87_out[1], xor_87_out[2], xor_87_out[3], xor_87_out[4], xor_87_out[5], xor_87_out[6]);
  // NOT_Gate not_91 has open pins: in=or_90_out, out=open
  or or_91 (or_91_out, xor_88_out[0], xor_88_out[1], xor_88_out[2], xor_88_out[3], xor_88_out[4], xor_88_out[5], xor_88_out[6]);
  not not_92 (not_92_out, or_91_out);
  or or_92 (or_92_out, xor_89_out[0], xor_89_out[1], xor_89_out[2]);
  not not_93 (not_93_out, or_92_out);
  or or_93 (or_93_out, xor_90_out[0], xor_90_out[1], xor_90_out[2], xor_90_out[3], xor_90_out[4], xor_90_out[5], xor_90_out[6]);
  // NOT_Gate not_94 has open pins: in=or_93_out, out=open
  or or_94 (or_94_out, xor_91_out[0], xor_91_out[1], xor_91_out[2], xor_91_out[3], xor_91_out[4], xor_91_out[5], xor_91_out[6]);
  not not_95 (not_95_out, or_94_out);
  or or_95 (or_95_out, xor_92_out[0], xor_92_out[1], xor_92_out[2]);
  not not_96 (not_96_out, or_95_out);
  or or_96 (or_96_out, xor_93_out[0], xor_93_out[1], xor_93_out[2], xor_93_out[3], xor_93_out[4], xor_93_out[5], xor_93_out[6]);
  // NOT_Gate not_97 has open pins: in=or_96_out, out=open
  or or_97 (or_97_out, xor_94_out[0], xor_94_out[1], xor_94_out[2], xor_94_out[3], xor_94_out[4], xor_94_out[5], xor_94_out[6]);
  not not_98 (not_98_out, or_97_out);
  or or_98 (or_98_out, xor_95_out[0], xor_95_out[1], xor_95_out[2]);
  not not_99 (not_99_out, or_98_out);
  or or_99 (or_99_out, xor_96_out[0], xor_96_out[1], xor_96_out[2], xor_96_out[3], xor_96_out[4], xor_96_out[5], xor_96_out[6]);
  not not_100 (not_100_out, or_99_out);
  and and_35 (is_sw, not_89_out, not_90_out);
  and and_36 (is_bne, not_92_out, not_93_out);
  and and_37 (is_bge, not_95_out, not_96_out);
  and and_38 (is_bgeu, not_98_out, not_99_out, not_100_out);
  assign xor_97_out = Instruction[6:0] ^ 7'b0010111;  // XOR_Gate xor_97, 7 bits wide
  assign xor_98_out = Instruction[14:12] ^ 3'b001;  // XOR_Gate xor_98, 3 bits wide
  assign xor_99_out = Instruction[31:25] ^ 7'b1010001;  // XOR_Gate xor_99, 7 bits wide
  assign xor_100_out = Instruction[6:0] ^ 7'b1101111;  // XOR_Gate xor_100, 7 bits wide
  assign xor_101_out = Instruction[14:12] ^ 3'b001;  // XOR_Gate xor_101, 3 bits wide
  assign xor_102_out = Instruction[31:25] ^ 7'b1010001;  // XOR_Gate xor_102, 7 bits wide
  assign xor_103_out = Instruction[6:0] ^ 7'b1010001;  // XOR_Gate xor_103, 7 bits wide
  assign xor_104_out = Instruction[14:12] ^ 3'b001;  // XOR_Gate xor_104, 3 bits wide
  assign xor_105_out = Instruction[31:25] ^ 7'b1010001;  // XOR_Gate xor_105, 7 bits wide
  assign xor_106_out = Instruction[6:0] ^ 7'b1010001;  // XOR_Gate xor_106, 7 bits wide
  assign xor_107_out = Instruction[14:12] ^ 3'b001;  // XOR_Gate xor_107, 3 bits wide
  assign xor_108_out = Instruction[31:25] ^ 7'b1010001;  // XOR_Gate xor_108, 7 bits wide
  or or_100 (or_100_out, xor_97_out[0], xor_97_out[1], xor_97_out[2], xor_97_out[3], xor_97_out[4], xor_97_out[5], xor_97_out[6]);
  or or_101 (or_101_out, xor_98_out[0], xor_98_out[1], xor_98_out[2]);
  or or_102 (or_102_out, xor_99_out[0], xor_99_out[1], xor_99_out[2], xor_99_out[3], xor_99_out[4], xor_99_out[5], xor_99_out[6]);
  or or_103 (or_103_out, xor_100_out[0], xor_100_out[1], xor_100_out[2], xor_100_out[3], xor_100_out[4], xor_100_out[5], xor_100_out[6]);
  or or_104 (or_104_out, xor_101_out[0], xor_101_out[1], xor_101_out[2]);
  or or_105 (or_105_out, xor_102_out[0], xor_102_out[1], xor_102_out[2], xor_102_out[3], xor_102_out[4], xor_102_out[5], xor_102_out[6]);
  or or_106 (or_106_out, xor_103_out[0], xor_103_out[1], xor_103_out[2], xor_103_out[3], xor_103_out[4], xor_103_out[5], xor_103_out[6]);
  or or_107 (or_107_out, xor_104_out[0], xor_104_out[1], xor_104_out[2]);
  or or_108 (or_108_out, xor_105_out[0], xor_105_out[1], xor_105_out[2], xor_105_out[3], xor_105_out[4], xor_105_out[5], xor_105_out[6]);
  or or_109 (or_109_out, xor_106_out[0], xor_106_out[1], xor_106_out[2], xor_106_out[3], xor_106_out[4], xor_106_out[5], xor_106_out[6]);
  or or_110 (or_110_out, xor_107_out[0], xor_107_out[1], xor_107_out[2]);
  or or_111 (or_111_out, xor_108_out[0], xor_108_out[1], xor_108_out[2], xor_108_out[3], xor_108_out[4], xor_108_out[5], xor_108_out[6]);
  not not_101 (not_101_out, or_100_out);
  // NOT_Gate not_102 has open pins: in=or_101_out, out=open
  // NOT_Gate not_103 has open pins: in=or_102_out, out=open
  not not_104 (not_104_out, or_103_out);
  // NOT_Gate not_105 has open pins: in=or_104_out, out=open
  // NOT_Gate not_106 has open pins: in=or_105_out, out=open
  not not_107 (not_107_out, or_106_out);
  not not_108 (not_108_out, or_107_out);
  not not_109 (not_109_out, or_108_out);
  not not_110 (not_110_out, or_109_out);
  not not_111 (not_111_out, or_110_out);
  not not_112 (not_112_out, or_111_out);
  buf and_39 (is_auipc, not_101_out);  // AND_Gate
  buf and_40 (is_jal, not_104_out);  // AND_Gate
  and and_41 (is_none1, not_107_out, not_108_out, not_109_out);
  and and_42 (is_none3, not_110_out, not_111_out, not_112_out);
  assign xor_109_out = Instruction[6:0] ^ 7'b0110111;  // XOR_Gate xor_109, 7 bits wide
  assign xor_110_out = Instruction[14:12] ^ 3'b001;  // XOR_Gate xor_110, 3 bits wide
  assign xor_111_out = Instruction[31:25] ^ 7'b1010001;  // XOR_Gate xor_111, 7 bits wide
  assign xor_112_out = Instruction[6:0] ^ 7'b1100111;  // XOR_Gate xor_112, 7 bits wide
  assign xor_113_out = Instruction[14:12] ^ 3'b000;  // XOR_Gate xor_113, 3 bits wide
  assign xor_114_out = Instruction[31:25] ^ 7'b1010001;  // XOR_Gate xor_114, 7 bits wide
  assign xor_115_out = Instruction[6:0] ^ 7'b1010001;  // XOR_Gate xor_115, 7 bits wide
  assign xor_116_out = Instruction[14:12] ^ 3'b001;  // XOR_Gate xor_116, 3 bits wide
  assign xor_117_out = Instruction[31:25] ^ 7'b1010001;  // XOR_Gate xor_117, 7 bits wide
  assign xor_118_out = Instruction[6:0] ^ 7'b1010001;  // XOR_Gate xor_118, 7 bits wide
  assign xor_119_out = Instruction[14:12] ^ 3'b001;  // XOR_Gate xor_119, 3 bits wide
  assign xor_120_out = Instruction[31:25] ^ 7'b1010001;  // XOR_Gate xor_120, 7 bits wide
  or or_112 (or_112_out, xor_109_out[0], xor_109_out[1], xor_109_out[2], xor_109_out[3], xor_109_out[4], xor_109_out[5], xor_109_out[6]);
  not not_113 (not_113_out, or_112_out);
  or or_113 (or_113_out, xor_110_out[0], xor_110_out[1], xor_110_out[2]);
  // NOT_Gate not_114 has open pins: in=or_113_out, out=open
  or or_114 (or_114_out, xor_111_out[0], xor_111_out[1], xor_111_out[2], xor_111_out[3], xor_111_out[4], xor_111_out[5], xor_111_out[6]);
  // NOT_Gate not_115 has open pins: in=or_114_out, out=open
  or or_115 (or_115_out, xor_112_out[0], xor_112_out[1], xor_112_out[2], xor_112_out[3], xor_112_out[4], xor_112_out[5], xor_112_out[6]);
  not not_116 (not_116_out, or_115_out);
  or or_116 (or_116_out, xor_113_out[0], xor_113_out[1], xor_113_out[2]);
  not not_117 (not_117_out, or_116_out);
  or or_117 (or_117_out, xor_114_out[0], xor_114_out[1], xor_114_out[2], xor_114_out[3], xor_114_out[4], xor_114_out[5], xor_114_out[6]);
  // NOT_Gate not_118 has open pins: in=or_117_out, out=open
  or or_118 (or_118_out, xor_115_out[0], xor_115_out[1], xor_115_out[2], xor_115_out[3], xor_115_out[4], xor_115_out[5], xor_115_out[6]);
  not not_119 (not_119_out, or_118_out);
  or or_119 (or_119_out, xor_116_out[0], xor_116_out[1], xor_116_out[2]);
  not not_120 (not_120_out, or_119_out);
  or or_120 (or_120_out, xor_117_out[0], xor_117_out[1], xor_117_out[2], xor_117_out[3], xor_117_out[4], xor_117_out[5], xor_117_out[6]);
  not not_121 (not_121_out, or_120_out);
  or or_121 (or_121_out, xor_118_out[0], xor_118_out[1], xor_118_out[2], xor_118_out[3], xor_118_out[4], xor_118_out[5], xor_118_out[6]);
  not not_122 (not_122_out, or_121_out);
  or or_122 (or_122_out, xor_119_out[0], xor_119_out[1], xor_119_out[2]);
  not not_123 (not_123_out, or_122_out);
  or or_123 (or_123_out, xor_120_out[0], xor_120_out[1], xor_120_out[2], xor_120_out[3], xor_120_out[4], xor_120_out[5], xor_120_out[6]);
  not not_124 (not_124_out, or_123_out);
  buf and_43 (is_lui, not_113_out);  // AND_Gate
  and and_44 (is_jalr, not_116_out, not_117_out);
  and and_45 (is_none2, not_119_out, not_120_out, not_121_out);
  and and_46 (is_none4, not_122_out, not_123_out, not_124_out);

  // Other names for the same wires on the sheet: opcode[6:0] = Instruction[6:0]; rd[4:0] = Instruction[11:7];
  //   funct3[2:0] = Instruction[14:12]; rs1[4:0] = Instruction[19:15]; rs2[4:0] = Instruction[24:20];
  //   funct7[6:0] = Instruction[31:25]

  // Notes on the sheet:
  //   0-8 function
  //   INPUTS to your circuit
  //   Connect ROM Input here ->
  //   contents of rom_1 (hex, n*v repeats v):
  //   1001 1401 1601 1081 1481 1591 1101 1201 1291 1681 1301 1381 41 41 41 1041 10c1 1141 1241 12d1 16c1
  //   1341 13c1 3842 3842 3842 4*3074 3064 3064 1067 17e7 2069 2041
  //   ROM FOR CONTROL LOGIC
  //   DON'T CHANGE THE LOCATIONS OF THE INPUTS AND OUTPUTS!
  //   This is only if you choose to do the ROM option
  //   CONNECT
  //   WIRE
  //   TO
  //   USE
  //   ROM
  //   OUTPUT from your circuit
  //   Reminder: If using ROM, use combinational logic for PCSel
  //   8-16 function
  //   16-24 function
  //   24-32 function
  //   32-35 function
endmodule
