// Logisim project cpu.circ as structural Verilog: 1 circuit, main circuit cpu
module cpu (
  input  clk,
  input  [31:0] Instruction,
  input  [31:0] MemReadData,
  output [31:0] MemAddress,
  output [31:0] ProgramCounter,
  output [31:0] ra,
  output [31:0] sp,
  output [31:0] t0,
  output [31:0] t1,
  output [31:0] t2,
  output [31:0] s0,
  output [31:0] s1,
  output [31:0] a0,
  output [3:0] MemWriteMask,
  output [31:0] MemWriteData
);

  wire branch_comp_1_breq, branch_comp_1_brlt, control_logic_1_asel, control_logic_1_brun,
       control_logic_1_bsel, control_logic_1_memwen, control_logic_1_pcsel, control_logic_1_regwen;
  wire [1:0] control_logic_1_wbsel;
  wire [2:0] control_logic_1_immsel, funct3;
  wire [3:0] control_logic_1_alusel;
  wire [31:0] adder_1_out, adder_2_out, immediate, Instruction2, Instruction_select, Memory,
       multiplexer_1_out, multiplexer_3_out, multiplexer_4_out, ProgramCounter2, read1, read2, WriteR;

  Adder #(.width(32)) adder_1 (.a(ProgramCounter), .b(32'h4), .out(adder_1_out));  // open: cin, cout
  Register #(.width(32)) register_1 (
    .D(Instruction_select), .clk(clk), .Q({Instruction2[31:15], funct3, Instruction2[11:0]}));  // open: en, clr
  Register #(.width(32)) PC (.D(multiplexer_1_out), .clk(clk), .Q(ProgramCounter));  // open: en, clr
  Multiplexer #(.width(32)) multiplexer_1 (
    .in0(MemAddress), .in1(adder_1_out), .out(multiplexer_1_out), .sel(control_logic_1_pcsel));
  Register #(.width(32)) register_2 (.D(ProgramCounter), .clk(clk), .Q(ProgramCounter2));  // open: en, clr
  control_logic control_logic_1 (
    .Instruction({Instruction2[31:15], funct3, Instruction2[11:0]}), .BrEq(branch_comp_1_breq),
    .BrLt(branch_comp_1_brlt), .PCSel(control_logic_1_pcsel), .RegWEn(control_logic_1_regwen),
    .ImmSel(control_logic_1_immsel), .BrUn(control_logic_1_brun), .ASel(control_logic_1_asel),
    .BSel(control_logic_1_bsel), .ALUSel(control_logic_1_alusel), .MemWEn(control_logic_1_memwen),
    .WBSel(control_logic_1_wbsel));
  regfile regfile_1 (
    .ReadIndex1(Instruction2[19:15]), .ReadIndex2(Instruction2[24:20]), .WriteIndex(Instruction2[11:7]),
    .WriteData(WriteR), .RegWEn(control_logic_1_regwen), .clk(clk), .ra(ra), .sp(sp), .t0(t0), .t1(t1),
    .t2(t2), .s0(s0), .s1(s1), .a0(a0), .ReadData1(read1), .ReadData2(read2));
  imm_gen imm_gen_1 (
    .Instruction({Instruction2[31:15], funct3, Instruction2[11:0]}), .ImmSel(control_logic_1_immsel),
    .Immediate(immediate));
  Multiplexer #(.width(32)) multiplexer_2 (
    .in0(32'h13), .in1(Instruction), .out(Instruction_select), .sel(control_logic_1_pcsel));
  branch_comp branch_comp_1 (
    .BrData1(read1), .BrData2(read2), .BrUn(control_logic_1_brun), .BrEq(branch_comp_1_breq),
    .BrLt(branch_comp_1_brlt));
  Multiplexer #(.width(32)) multiplexer_3 (
    .in0(read1), .in1(ProgramCounter2), .out(multiplexer_3_out), .sel(control_logic_1_asel));
  Multiplexer #(.width(32)) multiplexer_4 (
    .in0(read2), .in1(immediate), .out(multiplexer_4_out), .sel(control_logic_1_bsel));
  alu alu_1 (.A(multiplexer_3_out), .B(multiplexer_4_out), .ALUSel(control_logic_1_alusel), .ALUResult(MemAddress));
  Adder #(.width(32)) adder_2 (.a(ProgramCounter2), .b(32'h4), .out(adder_2_out));  // open: cin, cout
  partial_store partial_store_1 (
    .Instruction({Instruction2[31:15], funct3, Instruction2[11:0]}), .MemAddress(MemAddress),
    .DataFromReg(read2), .MemWEn(control_logic_1_memwen), .MemWriteMask(MemWriteMask),
    .DataToMem(MemWriteData));
  partial_load partial_load_1 (
    .Instruction({Instruction2[31:15], funct3, Instruction2[11:0]}), .MemAddress(MemAddress),
    .DataFromMem(MemReadData), .DataToReg(Memory));
  Multiplexer #(.select(2), .width(32)) multiplexer_5 (
    .in0(Memory), .in1(MemAddress), .in2(adder_2_out), .out(WriteR), .sel(control_logic_1_wbsel));  // open: in3

  // Other names for the same wires on the sheet: alu_result[31:0] = MemAddress; opcode[6:0] = Instruction2[6:0];
  //   rd[4:0] = Instruction2[11:7]; Instruction2[14:12] = funct3; rs1[4:0] = Instruction2[19:15];
  //   rs2[4:0] = Instruction2[24:20]

  // Notes on the sheet:
  //   To IMEM
  //   IMEM (do **NOT** move this)
  //   From IMEM
  //   Inputs/Outputs for testing. Do **NOT** move these.
  //   It is OK to move the PC, RegFile, ALU, MEM, Branch Comp, Imm Gen, Partial Load, Partial Store and Control Logic to wherever is most convenient for you when constructing your CPU, and to delete this text
  //   To DMEM
  //   DMEM (do **NOT** move this)
  //   From DMEM
endmodule
