// Logisim project imm-gen.circ as structural Verilog: 1 circuit, main circuit imm_gen
module imm_gen (
  input  [31:0] Instruction,
  input  [2:0] ImmSel,
  output [31:0] Immediate
);

  wire [31:11] I_imm, S_imm;
  wire [31:12] B_imm;
  wire [31:20] J_imm;

  assign I_imm = {{20{Instruction[31]}}, Instruction[31]};  // Bit_Extender bit_extender_1
  assign S_imm = {{20{Instruction[31]}}, Instruction[31]};  // Bit_Extender bit_extender_2
  assign B_imm = {{19{Instruction[31]}}, Instruction[31]};  // Bit_Extender bit_extender_3
  assign J_imm = {{11{Instruction[31]}}, Instruction[31]};  // Bit_Extender bit_extender_4
  Multiplexer #(.select(3), .width(32)) multiplexer_1 (
    .in0({I_imm, Instruction[30:20]}), .in1({S_imm, Instruction[30:25], Instruction[11:7]}),
    .in2({B_imm, Instruction[7], Instruction[30:25], Instruction[11:8], 1'b0}),
    .in3({Instruction[31:12], {12{1'b0}}}),
    .in4({J_imm, Instruction[19:12], Instruction[20], Instruction[30:21], 1'b0}), .out(Immediate),
    .sel(ImmSel));  // open: in5, in6, in7

  // Other names for the same wires on the sheet: B_imm[11:1] = {Instruction[7], Instruction[30:25], Instruction[11:8]};
  //   Inst11_7[4:0] = Instruction[11:7]; Inst11_8[3:0] = Instruction[11:8];
  //   S_imm[10:0] = {Instruction[30:25], Instruction[11:7]}; Inst7 = Instruction[7]; I_imm[10:0] = Instruction[30:20];
  //   Inst30_20[10:0] = Instruction[30:20]; Inst30_21[9:0] = Instruction[30:21]; Inst31_12[19:0] = Instruction[31:12];
  //   J_imm[19:1] = {Instruction[19:12], Instruction[20], Instruction[30:21]}; U_imm[31:12] = Instruction[31:12];
  //   Inst30_25[5:0] = Instruction[30:25]; Inst20 = Instruction[20]; Inst19_12[7:0] = Instruction[19:12];
  //   Inst31 = Instruction[31]

  // Notes on the sheet:
  //   INPUTS to your circuit
  //   DON'T CHANGE THE LOCATIONS OF THE INPUTS AND OUTPUTS!
  //   OUTPUT from your circuit
endmodule
