// Logisim project partial-store.circ as structural Verilog: 1 circuit, main circuit partial_store
module partial_store (
  input  [31:0] Instruction,
  input  [31:0] MemAddress,
  input  [31:0] DataFromReg,
  input  MemWEn,
  output [3:0] MemWriteMask,
  output [31:0] DataToMem
);

  wire [3:0] multiplexer_6_out, sb_mask, sh_mask;
  wire [31:0] bit_extender_1_out, bit_extender_2_out, multiplexer_5_out, sb, sh, shifter_1_out,
       shifter_2_out, shifter_3_out, shifter_4_out, shifter_5_out, shifter_6_out;

  assign bit_extender_1_out = {{24{DataFromReg[7]}}, DataFromReg[7:0]};  // Bit_Extender bit_extender_1
  assign bit_extender_2_out = {{16{DataFromReg[15]}}, DataFromReg[15:0]};  // Bit_Extender bit_extender_2
  Shifter #(.width(32)) shifter_1 (.in(bit_extender_1_out), .\dist ({5{1'b0}}), .out(shifter_1_out));
  Shifter #(.width(32)) shifter_2 (.in(bit_extender_1_out), .\dist (5'b01000), .out(shifter_2_out));
  Shifter #(.width(32)) shifter_3 (.in(bit_extender_1_out), .\dist (5'b10000), .out(shifter_3_out));
  Shifter #(.width(32)) shifter_4 (.in(bit_extender_1_out), .\dist (5'b11000), .out(shifter_4_out));
  Shifter #(.width(32)) shifter_5 (.in(bit_extender_2_out), .\dist ({5{1'b0}}), .out(shifter_5_out));
  Shifter #(.width(32)) shifter_6 (.in(bit_extender_2_out), .\dist (5'b10000), .out(shifter_6_out));
  Multiplexer #(.select(2), .width(32)) multiplexer_1 (
    .in0(shifter_1_out), .in1(shifter_2_out), .in2(shifter_3_out), .in3(shifter_4_out), .out(sb),
    .sel(MemAddress[1:0]));
  Multiplexer #(.select(2), .width(32)) multiplexer_2 (
    .in0(shifter_5_out), .in2(shifter_6_out), .out(sh), .sel(MemAddress[1:0]));  // open: in1, in3
  Multiplexer #(.select(2), .width(4)) multiplexer_3 (
    .in0(4'b0001), .in1(4'b0010), .in2(4'b0100), .in3(4'b1000), .out(sb_mask), .sel(MemAddress[1:0]));
  Multiplexer #(.select(2), .width(4)) multiplexer_4 (
    .in0(4'b0011), .in2(4'b1100), .out(sh_mask), .sel(MemAddress[1:0]));  // open: in1, in3
  Multiplexer #(.select(3), .width(32)) multiplexer_5 (
    .in0(sb), .in1(sh), .in2(DataFromReg), .out(multiplexer_5_out), .sel(Instruction[14:12]));  // open: in3, in4, in5, in6, in7
  Multiplexer #(.select(3), .width(4)) multiplexer_6 (
    .in0(sb_mask), .in1(sh_mask), .in2(4'b1111), .out(multiplexer_6_out), .sel(Instruction[14:12]));  // open: in3, in4, in5, in6, in7
  Multiplexer #(.width(32)) multiplexer_7 (.in0({32{1'b0}}), .in1(multiplexer_5_out), .out(DataToMem), .sel(MemWEn));
  Multiplexer #(.width(4)) multiplexer_8 (.in0(4'b0000), .in1(multiplexer_6_out), .out(MemWriteMask), .sel(MemWEn));

  // Other names for the same wires on the sheet: opcode[6:0] = Instruction[6:0]; rd[4:0] = Instruction[11:7];
  //   funct3[2:0] = Instruction[14:12]; rs1[4:0] = Instruction[19:15]; imm1[11:0] = Instruction[31:20];
  //   MemBottom[1:0] = MemAddress[1:0]; Data0_7[7:0] = DataFromReg[7:0]; Data0_15[15:0] = DataFromReg[15:0];
  //   sw[31:0] = DataFromReg

  // Notes on the sheet:
  //   INPUTS to your circuit
  //   DON'T CHANGE THE LOCATIONS OF THE INPUTS AND OUTPUTS!
  //   OUTPUT from your circuit
endmodule
