// Logisim project regfile.circ as structural Verilog: 1 circuit, main circuit regfile
module regfile (
  input  [4:0] ReadIndex1,
  input  [4:0] ReadIndex2,
  input  [4:0] WriteIndex,
  input  [31:0] WriteData,
  input  RegWEn,
  input  clk,
  output [31:0] ra,
  output [31:0] sp,
  output [31:0] t0,
  output [31:0] t1,
  output [31:0] t2,
  output [31:0] s0,
  output [31:0] s1,
  output [31:0] a0,
  output [31:0] ReadData1,
  output [31:0] ReadData2
);

  wire a0_w, a1_w, a2_w, a3_w, a4_w, a5_w, a6_w, a7_w, gp_w, ra_w, s0_w, s1_w, s2_w, s3_w, s4_w, s5_w, s6_w,
       s7_w, s8_w, s9_w, s10_w, s11_w, sp_w, t0_w, t1_w, t2_w, t3_w, t4_w, t5_w, t6_w, tp_w, x0_w;
  wire [31:0] a1, a2, a3, a4, a5, a6, a7, gp, s2, s3, s4, s5, s6, s7, s8, s9, s10, s11, t3, t4, t5, t6, tp;

  Multiplexer #(.select(5), .width(32)) multiplexer_1 (
    .in0({32{1'b0}}), .in1(ra), .in2(sp), .in3(gp), .in4(tp), .in5(t0), .in6(t1), .in7(t2), .in8(s0),
    .in9(s1), .in10(a0), .in11(a1), .in12(a2), .in13(a3), .in14(a4), .in15(a5), .in16(a6), .in17(a7),
    .in18(s2), .in19(s3), .in20(s4), .in21(s5), .in22(s6), .in23(s7), .in24(s8), .in25(s9), .in26(s10),
    .in27(s11), .in28(t3), .in29(t4), .in30(t5), .in31(t6), .out(ReadData1), .sel(ReadIndex1));
  Register #(.width(32)) register_1 (.D(WriteData), .en(ra_w), .clk(clk), .Q(ra));  // open: clr
  Register #(.width(32)) register_2 (.D(WriteData), .en(t2_w), .clk(clk), .Q(t2));  // open: clr
  Register #(.width(32)) register_3 (.D(WriteData), .en(a3_w), .clk(clk), .Q(a3));  // open: clr
  Register #(.width(32)) register_4 (.D(WriteData), .en(s3_w), .clk(clk), .Q(s3));  // open: clr
  Register #(.width(32)) register_5 (.D(WriteData), .en(s9_w), .clk(clk), .Q(s9));  // open: clr
  Register #(.width(32)) register_6 (.D(WriteData), .en(sp_w), .clk(clk), .Q(sp));  // open: clr
  Register #(.width(32)) register_7 (.D(WriteData), .en(s0_w), .clk(clk), .Q(s0));  // open: clr
  Register #(.width(32)) register_8 (.D(WriteData), .en(a4_w), .clk(clk), .Q(a4));  // open: clr
  Register #(.width(32)) register_9 (.D(WriteData), .en(s4_w), .clk(clk), .Q(s4));  // open: clr
  Register #(.width(32)) register_10 (.D(WriteData), .en(s10_w), .clk(clk), .Q(s10));  // open: clr
  Register #(.width(32)) register_11 (.D(WriteData), .en(gp_w), .clk(clk), .Q(gp));  // open: clr
  Register #(.width(32)) register_12 (.D(WriteData), .en(s1_w), .clk(clk), .Q(s1));  // open: clr
  Register #(.width(32)) register_13 (.D(WriteData), .en(a5_w), .clk(clk), .Q(a5));  // open: clr
  Register #(.width(32)) register_14 (.D(WriteData), .en(s5_w), .clk(clk), .Q(s5));  // open: clr
  Register #(.width(32)) register_15 (.D(WriteData), .en(s11_w), .clk(clk), .Q(s11));  // open: clr
  Multiplexer #(.select(5), .width(32)) multiplexer_2 (
    .in0({32{1'b0}}), .in1(ra), .in2(sp), .in3(gp), .in4(tp), .in5(t0), .in6(t1), .in7(t2), .in8(s0),
    .in9(s1), .in10(a0), .in11(a1), .in12(a2), .in13(a3), .in14(a4), .in15(a5), .in16(a6), .in17(a7),
    .in18(s2), .in19(s3), .in20(s4), .in21(s5), .in22(s6), .in23(s7), .in24(s8), .in25(s9), .in26(s10),
    .in27(s11), .in28(t3), .in29(t4), .in30(t5), .in31(t6), .out(ReadData2), .sel(ReadIndex2));
  Register #(.width(32)) register_16 (.D(WriteData), .en(tp_w), .clk(clk), .Q(tp));  // open: clr
  Register #(.width(32)) register_17 (.D(WriteData), .en(a0_w), .clk(clk), .Q(a0));  // open: clr
  Register #(.width(32)) register_18 (.D(WriteData), .en(a6_w), .clk(clk), .Q(a6));  // open: clr
  Register #(.width(32)) register_19 (.D(WriteData), .en(s6_w), .clk(clk), .Q(s6));  // open: clr
  Register #(.width(32)) register_20 (.D(WriteData), .en(t3_w), .clk(clk), .Q(t3));  // open: clr
  Register #(.width(32)) register_21 (.D(WriteData), .en(t0_w), .clk(clk), .Q(t0));  // open: clr
  Register #(.width(32)) register_22 (.D(WriteData), .en(a1_w), .clk(clk), .Q(a1));  // open: clr
  Register #(.width(32)) register_23 (.D(WriteData), .en(a7_w), .clk(clk), .Q(a7));  // open: clr
  Register #(.width(32)) register_24 (.D(WriteData), .en(s7_w), .clk(clk), .Q(s7));  // open: clr
  Register #(.width(32)) register_25 (.D(WriteData), .en(t4_w), .clk(clk), .Q(t4));  // open: clr
  Demultiplexer #(.select(5)) demultiplexer_1 (
    .out0(x0_w), .out1(ra_w), .out2(sp_w), .out3(gp_w), .out4(tp_w), .out5(t0_w), .out6(t1_w), .out7(t2_w),
    .out8(s0_w), .out9(s1_w), .out10(a0_w), .out11(a1_w), .out12(a2_w), .out13(a3_w), .out14(a4_w),
    .out15(a5_w), .out16(a6_w), .out17(a7_w), .out18(s2_w), .out19(s3_w), .out20(s4_w), .out21(s5_w),
    .out22(s6_w), .out23(s7_w), .out24(s8_w), .out25(s9_w), .out26(s10_w), .out27(s11_w), .out28(t3_w),
    .out29(t4_w), .out30(t5_w), .out31(t6_w), .in(RegWEn), .sel(WriteIndex));
  Register #(.width(32)) register_26 (.D(WriteData), .en(t1_w), .clk(clk), .Q(t1));  // open: clr
  Register #(.width(32)) register_27 (.D(WriteData), .en(a2_w), .clk(clk), .Q(a2));  // open: clr
  Register #(.width(32)) register_28 (.D(WriteData), .en(s2_w), .clk(clk), .Q(s2));  // open: clr
  Register #(.width(32)) register_29 (.D(WriteData), .en(s8_w), .clk(clk), .Q(s8));  // open: clr
  Register #(.width(32)) register_30 (.D(WriteData), .en(t5_w), .clk(clk), .Q(t5));  // open: clr
  Register #(.width(32)) register_31 (.D(WriteData), .en(t6_w), .clk(clk), .Q(t6));  // open: clr

  // Notes on the sheet:
  //   INPUTS to your circuit
  //   DON'T CHANGE THE LOCATIONS OF THE INPUTS AND OUTPUTS!
  //   These are DEBUG/TEST outputs from your circuit.
  //   OUTPUTS from your circuit
endmodule
